// Logisim project ButtonCounter.circ as structural Verilog: 2 circuits, main circuit Letter Decoder
module main (
  input  Button,
  input  Reset_Thing,
  output Dot_Dash_Pin,
  output Input_Space_Pin,
  output Letter_Space_Pin,
  output Word_Space_Pin
);

  wire and_1_out, and_2_out, clock_1_out, clock_2_out, d_ff_1_q, d_ff_2_q, d_ff_4_q, j_k_ff_1_q, j_k_ff_1_qn,
       not_1_out, not_2_out;
  wire [3:0] counter_1_q, counter_2_q;

  Clock clock_1 (.out(clock_1_out));
  Clock #(.highDuration(10), .lowDuration(10)) clock_2 (.out(clock_2_out));
  D_Flip_Flop d_ff_1 (.clk(clock_1_out), .D(Button), .Q(d_ff_1_q));  // open: Qn, preset, en, reset
  and and_1 (and_1_out, d_ff_1_q, clock_2_out);
  not not_1 (not_1_out, d_ff_1_q);
  Counter #(.width(4), .max('hf)) counter_1 (
    .Q(counter_1_q), .clk(clock_2_out), .clr(d_ff_1_q));  // open: load, D, count, carry
  Counter #(.width(4), .max('hf)) counter_2 (
    .Q(counter_2_q), .clk(and_1_out), .clr(not_1_out));  // open: load, D, count, carry
  J_K_Flip_Flop j_k_ff_1 (
    .J(1'b1), .clk(not_1_out), .K(1'b1), .Q(j_k_ff_1_q), .Qn(j_k_ff_1_qn), .en(1'b1), .reset(d_ff_2_q));  // open: preset
  and and_2 (and_2_out, counter_1_q[0], counter_1_q[3]);
  D_Flip_Flop d_ff_2 (
    .clk(d_ff_1_q), .D(j_k_ff_1_q), .Q(d_ff_2_q), .en(1'b1), .reset(j_k_ff_1_qn));  // open: Qn, preset
  D_Flip_Flop d_ff_3 (.clk(and_2_out), .D(1'b1), .Q(Word_Space_Pin), .reset(d_ff_1_q));  // open: Qn, preset, en
  D_Flip_Flop d_ff_4 (.clk(counter_1_q[2]), .D(1'b1), .Q(d_ff_4_q), .reset(d_ff_1_q));  // open: Qn, preset, en
  not not_2 (not_2_out, Word_Space_Pin);
  D_Flip_Flop d_ff_5 (.clk(counter_2_q[2]), .D(1'b1), .Q(Input_Space_Pin), .reset(d_ff_2_q));  // open: Qn, preset, en
  and and_3 (Letter_Space_Pin, d_ff_4_q, not_2_out);
  D_Flip_Flop d_ff_6 (
    .clk(j_k_ff_1_q), .D(Input_Space_Pin), .Q(Dot_Dash_Pin), .en(1'b1), .reset(Reset_Thing));  // open: Qn, preset

  // Notes on the sheet:
  //   Debouncer D FF
  //   On Counter
endmodule

module Letter_Decoder (
  input  in_1,
  input  in_2,
  input  in_3
);

  wire _4AND1_out, AND1_out, clock_1_out, clock_2_out, clock_3_out, D1_q, D2_qn, D3_q, d_ff_1_qn, d_ff_2_q,
       JK1_q, main_1_letter_space_pin, main_1_word_space_pin, multiplexer_1_out, N1_out, N2_out, not_1_out,
       not_2_out, not_3_out, not_4_out, not_5_out, OR1_out, OR2_out;
  wire [3:0] counter_1_q, counter_2_q;
  wire [4:0] shift_register_1_q3;
  wire [7:0] C3_q, ram_1_data;

  main main_1 (
    .Button(in_1), .Dot_Dash_Pin(shift_register_1_q3[4]), .Letter_Space_Pin(main_1_letter_space_pin),
    .Word_Space_Pin(main_1_word_space_pin), .Reset_Thing(counter_1_q[1]));  // open: Input_Space_Pin
  not not_1 (not_1_out, main_1_word_space_pin);
  not not_2 (not_2_out, not_1_out);
  Counter C3 (.Q(C3_q), .clk(multiplexer_1_out), .clr(OR2_out));  // open: load, D, count, carry
  or OR1 (OR1_out, main_1_letter_space_pin, d_ff_2_q);
  D_Flip_Flop D1 (.clk(clock_2_out), .D(not_2_out), .Q(D1_q), .reset(d_ff_2_q));  // open: Qn, preset, en
  not not_3 (not_3_out, D1_q);
  not not_4 (not_4_out, not_3_out);
  Clock clock_1 (.out(clock_1_out));
  D_Flip_Flop d_ff_1 (
    .clk(main_1_letter_space_pin), .D(1'b1), .Qn(d_ff_1_qn), .reset(counter_1_q[2]));  // open: Q, preset, en
  and AND1 (AND1_out, OR1_out, D2_qn);
  Multiplexer #(.enable("false")) multiplexer_1 (
    .in0(AND1_out), .in1(clock_3_out), .out(multiplexer_1_out), .sel(JK1_q));
  D_Flip_Flop d_ff_2 (.clk(not_4_out), .D(1'b1), .Q(d_ff_2_q), .reset(not_1_out));  // open: Qn, preset, en
  Counter #(.width(4), .max('hf)) counter_1 (
    .Q(counter_1_q), .clk(clock_1_out), .clr(d_ff_1_qn));  // open: load, D, count, carry
  Counter #(.width(4), .max('hf)) counter_2 (
    .Q(counter_2_q), .clk(in_1), .clr(counter_1_q[1]));  // open: load, D, count, carry
  RAM #(.bus("asynch")) ram_1 (.addr(C3_q), .data(ram_1_data), .ld(not_5_out));  // open: sel, clr
  not not_5 (not_5_out, D2_qn);
  or OR2 (OR2_out, D3_q, _4AND1_out);
  Clock clock_2 (.out(clock_2_out));
  Shift_Register #(.length(4)) shift_register_1 (
    .in(shift_register_1_q3[4]), .clk(N1_out), .clr(counter_1_q[1]), .q0(shift_register_1_q3[3]),
    .q1(shift_register_1_q3[2]), .q2(shift_register_1_q3[1]), .q3(shift_register_1_q3[0]));  // open: shift, out, load, d0, d1, d2, d3
  not N1 (N1_out, in_1);
  assign ram_1_data = D2_qn ? {counter_2_q[2:0], shift_register_1_q3} : 8'bz;  // Controlled_Buffer _4MUX_1_2
  D_Flip_Flop D3 (.clk(clock_2_out), .D(in_3), .Q(D3_q));  // open: Qn, preset, en, reset
  Clock #(.highDuration(20), .lowDuration(20)) clock_3 (.out(clock_3_out));
  not N2 (N2_out, ram_1_data[2]);
  J_K_Flip_Flop JK1 (.J(1'b1), .clk(D3_q), .K(1'b1), .Q(JK1_q), .reset(_4AND1_out));  // open: Qn, preset, en
  and _4AND1 (_4AND1_out, ram_1_data[1], ram_1_data[5], ram_1_data[7], N2_out);
  ROM #(.dataWidth(6)) rom_1 (.addr(ram_1_data));  // open: data, sel
  D_Flip_Flop D2 (.clk(_4AND1_out), .D(1'b1), .Qn(D2_qn), .reset(in_2));  // open: Q, preset, en

  // Notes on the sheet:
  //   Counter 1
  //   C3
  //   RAM
  //   C2
  //   Note: Could've used XOR and AND and an OR instead of Mux but elected to use mux
  //   SR1
  //   EPROM
endmodule
